// Logisim project Lab5.circ as structural Verilog: 1 circuit, main circuit main
module main (
  input  A,
  input  B,
  input  C,
  input  D,
  output a_2,
  output b_2,
  output c_2,
  output d_2,
  output e,
  output f,
  output g
);

  wire and_1_out, and_2_out, and_3_out, and_4_out, and_5_out, and_6_out, and_7_out, and_8_out, and_9_out,
       and_10_out, and_11_out, and_12_out, and_13_out, nand_1_out, nand_2_out, nand_3_out, nand_4_out,
       nand_5_out, nand_6_out, nand_7_out, nand_8_out, nand_9_out, nand_10_out, nand_11_out, nand_12_out,
       nand_13_out, nand_14_out, nand_15_out, nand_16_out, nand_17_out, nand_18_out, nand_19_out,
       nand_20_out, nand_21_out, nand_22_out, nand_23_out, nand_24_out, nand_25_out, not_1_out, not_2_out,
       not_3_out, not_4_out, not_5_out, not_6_out, not_7_out, or_1_out, or_2_out, or_3_out, or_4_out,
       or_6_out;

  nand nand_1 (nand_1_out, B, B);
  nand nand_2 (nand_2_out, D, D);
  nand nand_3 (nand_3_out, B, B);
  not not_1 (not_1_out, B);
  not not_2 (not_2_out, C);
  and and_1 (and_1_out, not_2_out, not_3_out);
  not not_3 (not_3_out, D);
  and and_2 (and_2_out, C, D);
  not not_4 (not_4_out, C);
  or or_1 (or_1_out, not_4_out, D);
  or or_2 (or_2_out, B, A);
  nand nand_4 (nand_4_out, B, B);
  nand nand_5 (nand_5_out, D, D);
  nand nand_6 (nand_6_out, B, B);
  nand nand_7 (nand_7_out, C, C);
  not not_5 (not_5_out, B);
  and and_3 (and_3_out, not_5_out, not_6_out);
  not not_6 (not_6_out, D);
  and and_4 (and_4_out, C, not_7_out);
  not not_7 (not_7_out, D);
  nand nand_8 (nand_8_out, C, C);
  nand nand_9 (nand_9_out, D, D);
  nand nand_10 (nand_10_out, C, C);
  nand nand_11 (nand_11_out, B, B);
  nand nand_12 (nand_12_out, nand_1_out, nand_2_out);
  nand nand_13 (nand_13_out, nand_3_out, C);
  nand nand_14 (nand_14_out, B, D);
  nand nand_15 (nand_15_out, A, A);
  or or_3 (or_3_out, not_1_out, and_1_out);
  or or_4 (or_4_out, and_2_out, A);
  or or_5 (c_2, or_1_out, or_2_out);
  nand nand_16 (nand_16_out, nand_4_out, nand_5_out);
  nand nand_17 (nand_17_out, nand_6_out, C);
  nand nand_18 (nand_18_out, D, D);
  and and_5 (and_5_out, B, nand_7_out);
  or or_6 (or_6_out, and_3_out, and_4_out);
  and and_6 (and_6_out, A, B);
  nand nand_19 (nand_19_out, nand_8_out, nand_9_out);
  nand nand_20 (nand_20_out, B, B);
  and and_7 (and_7_out, nand_10_out, nand_11_out);
  nand nand_21 (nand_21_out, A, A);
  and and_8 (and_8_out, nand_12_out, nand_13_out);
  and and_9 (and_9_out, nand_14_out, nand_15_out);
  or or_7 (b_2, or_3_out, or_4_out);
  and and_10 (and_10_out, nand_16_out, nand_17_out);
  nand nand_22 (nand_22_out, C, nand_18_out);
  nand nand_23 (nand_23_out, and_5_out, D);
  nand nand_24 (nand_24_out, A, A);
  or or_8 (e, or_6_out, and_6_out);
  and and_11 (and_11_out, nand_19_out, nand_20_out);
  nand nand_25 (nand_25_out, A, A);
  nand nand_26 (g, and_7_out, nand_21_out);
  nand nand_27 (a_2, and_8_out, and_9_out);
  and and_12 (and_12_out, and_10_out, nand_22_out);
  and and_13 (and_13_out, nand_23_out, nand_24_out);
  nand nand_28 (f, and_11_out, nand_25_out);
  nand nand_29 (d_2, and_12_out, and_13_out);
endmodule
